// Logisim project dsdlab_CLAadder.circ as structural Verilog: 1 circuit, main circuit main
module main (
  input  c0,
  input  x0,
  input  y0,
  input  x1,
  input  y1,
  input  x2,
  input  y2,
  input  x3,
  input  y3,
  output s0,
  output c1,
  output s1,
  output c2,
  output s2,
  output c3,
  output s3,
  output c4
);

  wire and_1_out, and_2_out, and_3_out, and_4_out, and_5_out, and_6_out, and_7_out, and_8_out, and_9_out,
       and_10_out, and_11_out, and_12_out, p2g1_out, p3g2_out, xor_1_out, xor_2_out, xor_3_out, xor_4_out;

  xor xor_1 (xor_1_out, x0, y0);
  and and_1 (and_1_out, x0, y0);
  xor xor_2 (xor_2_out, x1, y1);
  and and_2 (and_2_out, y1, y1);
  xor xor_3 (xor_3_out, x2, y2);
  and and_3 (and_3_out, x2, y2);
  xor xor_4 (xor_4_out, x3, y3);
  and and_4 (and_4_out, x3, y3);
  and and_5 (and_5_out, c0, xor_1_out);
  and p2g1 (p2g1_out, and_2_out, xor_3_out);
  and p3g2 (p3g2_out, and_3_out, xor_4_out);
  and and_6 (and_6_out, xor_4_out, xor_3_out, and_3_out);
  and and_7 (and_7_out, and_1_out, xor_2_out);
  and and_8 (and_8_out, c0, xor_1_out, xor_2_out);
  and and_9 (and_9_out, xor_3_out, xor_2_out, and_1_out);
  or or_1 (c1, and_5_out, and_1_out);
  and and_10 (and_10_out, xor_4_out, xor_3_out, xor_2_out, and_1_out);
  and and_11 (and_11_out, and_8_out, xor_3_out);
  or or_2 (c2, and_7_out, and_8_out, and_2_out);
  and and_12 (and_12_out, and_11_out, xor_4_out);
  or or_3 (c3, and_11_out, p2g1_out, and_9_out, and_3_out);
  xor xor_5 (s0, xor_1_out, c0);
  xor xor_6 (s1, xor_2_out, c1);
  xor xor_7 (s2, xor_3_out, c2);
  or or_4 (c4, p3g2_out, and_10_out, and_12_out, and_6_out, and_4_out);
  xor xor_8 (s3, xor_4_out, c3);

  // Notes on the sheet:
  //   p1=x1 xor y1
  //   g1=x1y1
  //   p2=x2 xor y2
  //   g2=x2y2
  //   p3=x3 xor y3
  //   g3=x3y3
  //   p0=x0 xor y0
  //   g0=x0y0
  //   p0c0
  //   p3p2g1
  //   p1g0
  //   c0p0p1
  //   p2p1g0
  //   g0+p0c0
  //   p2p1p0c0
  //   p3p2p1g0
  //   g1+p1g0+p1p0c0
  //   p3p2p1p0c0
endmodule
